# Fritzing sketch 워킹목업 회로도 (saved by Fritzing 0.9.3b)
breadboards: 1

parts:
  부품1 = Arduino Uno (Rev3)
  부품2 = Arduino Uno (Rev3)
  S10 = Momentary Switch [package=ksa_sealed_tac_switch]
  S11 = Momentary Switch [package=ksa_sealed_tac_switch]
  S12 = Momentary Switch [package=ksa_sealed_tac_switch]
  S13 = Momentary Switch [package=ksa_sealed_tac_switch]
  S14 = Momentary Switch [package=ksa_sealed_tac_switch]
  S15 = Momentary Switch [package=ksa_sealed_tac_switch]
  S16 = Momentary Switch [package=ksa_sealed_tac_switch]
  S17 = Momentary Switch [package=ksa_sealed_tac_switch]
  S18 = Momentary Switch [package=ksa_sealed_tac_switch]
  R1 = Resistor [tolerance=±5% resistance=220 package=THT]
  R2 = Resistor [tolerance=±5% resistance=220 package=THT]
  R3 = Resistor [tolerance=±5% resistance=220 package=THT]
  R4 = Resistor [tolerance=±5% resistance=220 package=THT]
  R5 = Resistor [tolerance=±5% resistance=220 package=THT]
  R6 = Resistor [tolerance=±5% resistance=220 package=THT]
  R7 = Resistor [tolerance=±5% resistance=220 package=THT]
  R8 = Resistor [tolerance=±5% resistance=220 package=THT]
  R9 = Resistor [tolerance=±5% resistance=220 package=THT]
  U1 = OP482 - Low Power, High Speed JFET Quad Operational Amplifier [part_number=OP482]

nets:
  N1: 부품1.A4/SDA, 부품2.A4/SDA
  N2: 부품1.A5/SCL, 부품2.A5/SCL
  N3: 부품1.D9_PWM, S15.1
  N4: 부품1.D10_PWM/SS, S13.1
  N5: 부품1.D11_PWM/MOSI, S14.1
  N6: 부품1.D2, S10.1
  N7: 부품1.D3_PWM, S11.1
  N8: 부품1.D4, S12.1
  N9: 부품1.D5_PWM, S18.1
  N10: 부품1.D6_PWM, S16.1
  N11: 부품1.D7, S17.1
  N12: 부품1.5V, S10.4, S11.4, S12.4, S13.4, S14.4, S15.4, S16.4, S17.4, S18.4
  N13: 부품1.GND, R1.Pin_1, R2.Pin_1, R3.Pin_1, R4.Pin_1, R5.Pin_1, R6.Pin_1, R7.Pin_1, R8.Pin_1, R9.Pin_1
  N14: 부품2.D0/RX, U1.V-
  N15: 부품2.D1/TX, U1.+IND
  N16: 부품2.3V3, U1.+INA
  N17: 부품2.5V, U1.OUTA, U1.OUTD
  N18: 부품2.GND, U1.-INA, U1.-IND
  N19: S10.2, R1.Pin_0
  N20: S11.2, R9.Pin_0
  N21: S12.2, R8.Pin_0
  N22: S13.2, R3.Pin_0
  N23: S14.2, R2.Pin_0
  N24: S15.2, R4.Pin_0
  N25: S16.2, R6.Pin_0
  N26: S17.2, R5.Pin_0
  N27: S18.2, R7.Pin_0
